// Logisim project uuula1.circ as structural Verilog
module main (
  input  [31:0] Dado32,
  input  SelExterno,
  input  in_3,
  input  [4:0] SelRW,
  input  [4:0] SelRB,
  input  [3:0] CodOperacao,
  input  [4:0] SelRA
);

  wire [31:0] bancoregistrador_32_1_reg_a, bancoregistrador_32_1_reg_b, ula_32_1_resultado;

  bancoRegistrador_32 bancoregistrador_32_1 (
    .Externo(SelExterno), .Clock(in_3), .DadoExt(Dado32), .DATAin(ula_32_1_resultado), .Seletor(SelRW),
    .SELREG_A(SelRA), .SELREG_B(SelRB), .REG_A(bancoregistrador_32_1_reg_a),
    .REG_B(bancoregistrador_32_1_reg_b));
  ULA_32 ula_32_1 (
    .A(bancoregistrador_32_1_reg_a), .B(bancoregistrador_32_1_reg_b), .Resultado(ula_32_1_resultado),
    .CodigoOperacao(CodOperacao));  // open: out_4
endmodule

module ULACell (
  input  a,
  input  b,
  input  [3:0] in_3,
  input  Vem1,
  output out_5,
  output Vai1
);

  wire and_1_out, c_2_detect_1_s, complemento2_1_saida, nand_1_out, or_1_out, somadorcompleto_1_soma,
       xor_1_out;

  Complemento2 complemento2_1 (.B(b), .Saida(complemento2_1_saida), .Seletor(c_2_detect_1_s));
  SomadorCompleto somadorcompleto_1 (
    .vai1(Vai1), .b(complemento2_1_saida), .a(a), .soma(somadorcompleto_1_soma), .vem1(Vem1));
  C_2_detect c_2_detect_1 (.S(c_2_detect_1_s), .Codigo_operacao(in_3));
  and and_1 (and_1_out, a, b);
  or or_1 (or_1_out, a, b);
  xor xor_1 (xor_1_out, a, b);
  nand nand_1 (nand_1_out, a, b);
  mux_16 mux_16_1 (
    .Canal0(and_1_out), .Canal1(or_1_out), .Canal2(xor_1_out), .Canal3(somadorcompleto_1_soma), .Canal4(b),
    .Canal5(b), .Canal6(b), .Canal7(b), .Canal8(a), .Canal9(nand_1_out), .Canal15(somadorcompleto_1_soma),
    .Seletor3(in_3[3]), .Seletor2(in_3[2]), .Seletor1(in_3[1]), .Seletor0(in_3[0]), .Saida(out_5));  // open: Canal10, Canal11, Canal12, Canal13, Canal14
endmodule

// MUX-8
module mux_8 (
  input  Canal0,
  input  Canal1,
  input  Canal2,
  input  Canal3,
  input  Canal4,
  input  Canal5,
  input  Canal6,
  input  Canal7,
  input  Seletor_2,
  input  Seletor_1,
  input  Seletor_0,
  output out_12
);

  wire and_1_out, and_2_out, and_3_out, and_4_out, and_5_out, and_6_out, and_7_out, and_8_out;

  and and_1 (and_1_out, Canal0, ~Seletor_2, ~Seletor_1, ~Seletor_0);  // AND_Gate
  and and_2 (and_2_out, Canal1, ~Seletor_2, ~Seletor_1, Seletor_0);  // AND_Gate
  and and_3 (and_3_out, Canal2, ~Seletor_2, Seletor_1, ~Seletor_0);  // AND_Gate
  and and_4 (and_4_out, Canal3, ~Seletor_2, Seletor_1, Seletor_0);  // AND_Gate
  and and_5 (and_5_out, Canal4, Seletor_2, ~Seletor_1, ~Seletor_0);  // AND_Gate
  and and_6 (and_6_out, Canal5, Seletor_2, ~Seletor_1, Seletor_0);  // AND_Gate
  and and_7 (and_7_out, Canal6, Seletor_2, Seletor_1, ~Seletor_0);  // AND_Gate
  and and_8 (and_8_out, Canal7, Seletor_2, Seletor_1, Seletor_0);
  or or_1 (out_12, and_1_out, and_2_out, and_3_out, and_4_out, and_5_out, and_6_out, and_7_out, and_8_out);
endmodule

// ULA
module ULA_32 (
  input  [31:0] A,
  input  [3:0] CodigoOperacao,
  input  [31:0] B,
  output out_4,
  output [31:0] Resultado
);

  wire c_2_detect_1_s, lua_detect_1_out_2, sll_detect_1_out_2, sra_detect_1_out_2, srl_detect_1_out_2,
       ulacell_2_vai1, ulacell_3_vai1, ulacell_4_vai1, ulacell_5_vai1, ulacell_6_vai1, ulacell_7_vai1,
       ulacell_8_vai1, ulacell_9_vai1, ulacell_10_vai1, ulacell_11_vai1, ulacell_12_vai1, ulacell_13_vai1,
       ulacell_14_vai1, ulacell_15_vai1, ulacell_16_vai1, ulacell_17_vai1, ulacell_18_vai1, ulacell_19_vai1,
       ulacell_20_vai1, ulacell_21_vai1, ulacell_22_vai1, ulacell_23_vai1, ulacell_24_vai1, ulacell_25_vai1,
       ulacell_26_vai1, ulacell_27_vai1, ulacell_28_vai1, ulacell_29_vai1, ulacell_30_vai1, ulacell_31_vai1,
       ulacell_32_vai1;
  wire [31:0] lua_32_1_saida_lua_32bit, sll_32_1_saida_sll_32bit, sra_32_1_saida_sra_32bit,
       srl_32_1_saida_srl_32bit;

  sll_32 sll_32_1 (.in_1(B), .shift(sll_detect_1_out_2), .Saida_SLL_32BIT(sll_32_1_saida_sll_32bit));
  sll_detect sll_detect_1 (.out_2(sll_detect_1_out_2), .in_1(CodigoOperacao));
  lua_detect lua_detect_1 (.out_2(lua_detect_1_out_2), .in_1(CodigoOperacao));
  srl_32 srl_32_1 (
    .in_1(sll_32_1_saida_sll_32bit), .shift(srl_detect_1_out_2), .Saida_SRL_32BIT(srl_32_1_saida_srl_32bit));
  sra_32 sra_32_1 (
    .in_1(srl_32_1_saida_srl_32bit), .shift(sra_detect_1_out_2), .Saida_SRA_32BIT(sra_32_1_saida_sra_32bit));
  sra_detect sra_detect_1 (.out_2(sra_detect_1_out_2), .in_1(CodigoOperacao));
  srl_detect srl_detect_1 (.out_2(srl_detect_1_out_2), .in_1(CodigoOperacao));
  lua_32 lua_32_1 (.in_1(A), .shift(lua_detect_1_out_2), .Saida_LUA_32BIT(lua_32_1_saida_lua_32bit));
  ULACell ulacell_1 (
    .Vai1(out_4), .a(lua_32_1_saida_lua_32bit[31]), .b(sra_32_1_saida_sra_32bit[31]), .in_3(CodigoOperacao),
    .out_5(Resultado[31]), .Vem1(ulacell_2_vai1));
  ULACell ulacell_2 (
    .Vai1(ulacell_2_vai1), .a(lua_32_1_saida_lua_32bit[30]), .b(sra_32_1_saida_sra_32bit[30]),
    .in_3(CodigoOperacao), .out_5(Resultado[30]), .Vem1(ulacell_3_vai1));
  ULACell ulacell_3 (
    .Vai1(ulacell_3_vai1), .a(lua_32_1_saida_lua_32bit[29]), .b(sra_32_1_saida_sra_32bit[29]),
    .in_3(CodigoOperacao), .out_5(Resultado[29]), .Vem1(ulacell_4_vai1));
  ULACell ulacell_4 (
    .Vai1(ulacell_4_vai1), .a(lua_32_1_saida_lua_32bit[28]), .b(sra_32_1_saida_sra_32bit[28]),
    .in_3(CodigoOperacao), .out_5(Resultado[28]), .Vem1(ulacell_5_vai1));
  ULACell ulacell_5 (
    .Vai1(ulacell_5_vai1), .a(lua_32_1_saida_lua_32bit[27]), .b(sra_32_1_saida_sra_32bit[27]),
    .in_3(CodigoOperacao), .out_5(Resultado[27]), .Vem1(ulacell_6_vai1));
  ULACell ulacell_6 (
    .Vai1(ulacell_6_vai1), .a(lua_32_1_saida_lua_32bit[26]), .b(sra_32_1_saida_sra_32bit[26]),
    .in_3(CodigoOperacao), .out_5(Resultado[26]), .Vem1(ulacell_7_vai1));
  ULACell ulacell_7 (
    .Vai1(ulacell_7_vai1), .a(lua_32_1_saida_lua_32bit[25]), .b(sra_32_1_saida_sra_32bit[25]),
    .in_3(CodigoOperacao), .out_5(Resultado[25]), .Vem1(ulacell_8_vai1));
  ULACell ulacell_8 (
    .Vai1(ulacell_8_vai1), .a(lua_32_1_saida_lua_32bit[24]), .b(sra_32_1_saida_sra_32bit[24]),
    .in_3(CodigoOperacao), .out_5(Resultado[24]), .Vem1(ulacell_9_vai1));
  ULACell ulacell_9 (
    .Vai1(ulacell_9_vai1), .a(lua_32_1_saida_lua_32bit[23]), .b(sra_32_1_saida_sra_32bit[23]),
    .in_3(CodigoOperacao), .out_5(Resultado[23]), .Vem1(ulacell_10_vai1));
  ULACell ulacell_10 (
    .Vai1(ulacell_10_vai1), .a(lua_32_1_saida_lua_32bit[22]), .b(sra_32_1_saida_sra_32bit[22]),
    .in_3(CodigoOperacao), .out_5(Resultado[22]), .Vem1(ulacell_11_vai1));
  ULACell ulacell_11 (
    .Vai1(ulacell_11_vai1), .a(lua_32_1_saida_lua_32bit[21]), .b(sra_32_1_saida_sra_32bit[21]),
    .in_3(CodigoOperacao), .out_5(Resultado[21]), .Vem1(ulacell_12_vai1));
  ULACell ulacell_12 (
    .Vai1(ulacell_12_vai1), .a(lua_32_1_saida_lua_32bit[20]), .b(sra_32_1_saida_sra_32bit[20]),
    .in_3(CodigoOperacao), .out_5(Resultado[20]), .Vem1(ulacell_13_vai1));
  ULACell ulacell_13 (
    .Vai1(ulacell_13_vai1), .a(lua_32_1_saida_lua_32bit[19]), .b(sra_32_1_saida_sra_32bit[19]),
    .in_3(CodigoOperacao), .out_5(Resultado[19]), .Vem1(ulacell_14_vai1));
  ULACell ulacell_14 (
    .Vai1(ulacell_14_vai1), .a(lua_32_1_saida_lua_32bit[18]), .b(sra_32_1_saida_sra_32bit[18]),
    .in_3(CodigoOperacao), .out_5(Resultado[18]), .Vem1(ulacell_15_vai1));
  ULACell ulacell_15 (
    .Vai1(ulacell_15_vai1), .a(lua_32_1_saida_lua_32bit[17]), .b(sra_32_1_saida_sra_32bit[17]),
    .in_3(CodigoOperacao), .out_5(Resultado[17]), .Vem1(ulacell_16_vai1));
  ULACell ulacell_16 (
    .Vai1(ulacell_16_vai1), .a(lua_32_1_saida_lua_32bit[16]), .b(sra_32_1_saida_sra_32bit[16]),
    .in_3(CodigoOperacao), .out_5(Resultado[16]), .Vem1(ulacell_17_vai1));
  ULACell ulacell_17 (
    .Vai1(ulacell_17_vai1), .a(lua_32_1_saida_lua_32bit[15]), .b(sra_32_1_saida_sra_32bit[15]),
    .in_3(CodigoOperacao), .out_5(Resultado[15]), .Vem1(ulacell_18_vai1));
  ULACell ulacell_18 (
    .Vai1(ulacell_18_vai1), .a(lua_32_1_saida_lua_32bit[14]), .b(sra_32_1_saida_sra_32bit[14]),
    .in_3(CodigoOperacao), .out_5(Resultado[14]), .Vem1(ulacell_19_vai1));
  ULACell ulacell_19 (
    .Vai1(ulacell_19_vai1), .a(lua_32_1_saida_lua_32bit[13]), .b(sra_32_1_saida_sra_32bit[13]),
    .in_3(CodigoOperacao), .out_5(Resultado[13]), .Vem1(ulacell_20_vai1));
  ULACell ulacell_20 (
    .Vai1(ulacell_20_vai1), .a(lua_32_1_saida_lua_32bit[12]), .b(sra_32_1_saida_sra_32bit[12]),
    .in_3(CodigoOperacao), .out_5(Resultado[12]), .Vem1(ulacell_21_vai1));
  ULACell ulacell_21 (
    .Vai1(ulacell_21_vai1), .a(lua_32_1_saida_lua_32bit[11]), .b(sra_32_1_saida_sra_32bit[11]),
    .in_3(CodigoOperacao), .out_5(Resultado[11]), .Vem1(ulacell_22_vai1));
  ULACell ulacell_22 (
    .Vai1(ulacell_22_vai1), .a(lua_32_1_saida_lua_32bit[10]), .b(sra_32_1_saida_sra_32bit[10]),
    .in_3(CodigoOperacao), .out_5(Resultado[10]), .Vem1(ulacell_23_vai1));
  ULACell ulacell_23 (
    .Vai1(ulacell_23_vai1), .a(lua_32_1_saida_lua_32bit[9]), .b(sra_32_1_saida_sra_32bit[9]),
    .in_3(CodigoOperacao), .out_5(Resultado[9]), .Vem1(ulacell_24_vai1));
  ULACell ulacell_24 (
    .Vai1(ulacell_24_vai1), .a(lua_32_1_saida_lua_32bit[8]), .b(sra_32_1_saida_sra_32bit[8]),
    .in_3(CodigoOperacao), .out_5(Resultado[8]), .Vem1(ulacell_25_vai1));
  ULACell ulacell_25 (
    .Vai1(ulacell_25_vai1), .a(lua_32_1_saida_lua_32bit[7]), .b(sra_32_1_saida_sra_32bit[7]),
    .in_3(CodigoOperacao), .out_5(Resultado[7]), .Vem1(ulacell_26_vai1));
  ULACell ulacell_26 (
    .Vai1(ulacell_26_vai1), .a(lua_32_1_saida_lua_32bit[6]), .b(sra_32_1_saida_sra_32bit[6]),
    .in_3(CodigoOperacao), .out_5(Resultado[6]), .Vem1(ulacell_27_vai1));
  ULACell ulacell_27 (
    .Vai1(ulacell_27_vai1), .a(lua_32_1_saida_lua_32bit[5]), .b(sra_32_1_saida_sra_32bit[5]),
    .in_3(CodigoOperacao), .out_5(Resultado[5]), .Vem1(ulacell_28_vai1));
  ULACell ulacell_28 (
    .Vai1(ulacell_28_vai1), .a(lua_32_1_saida_lua_32bit[4]), .b(sra_32_1_saida_sra_32bit[4]),
    .in_3(CodigoOperacao), .out_5(Resultado[4]), .Vem1(ulacell_29_vai1));
  ULACell ulacell_29 (
    .Vai1(ulacell_29_vai1), .a(lua_32_1_saida_lua_32bit[3]), .b(sra_32_1_saida_sra_32bit[3]),
    .in_3(CodigoOperacao), .out_5(Resultado[3]), .Vem1(ulacell_30_vai1));
  ULACell ulacell_30 (
    .Vai1(ulacell_30_vai1), .a(lua_32_1_saida_lua_32bit[2]), .b(sra_32_1_saida_sra_32bit[2]),
    .in_3(CodigoOperacao), .out_5(Resultado[2]), .Vem1(ulacell_31_vai1));
  ULACell ulacell_31 (
    .Vai1(ulacell_31_vai1), .a(lua_32_1_saida_lua_32bit[1]), .b(sra_32_1_saida_sra_32bit[1]),
    .in_3(CodigoOperacao), .out_5(Resultado[1]), .Vem1(ulacell_32_vai1));
  C_2_detect c_2_detect_1 (.S(c_2_detect_1_s), .Codigo_operacao(CodigoOperacao));
  ULACell ulacell_32 (
    .Vai1(ulacell_32_vai1), .a(lua_32_1_saida_lua_32bit[0]), .b(sra_32_1_saida_sra_32bit[0]),
    .in_3(CodigoOperacao), .out_5(Resultado[0]), .Vem1(c_2_detect_1_s));
endmodule

module Somador (
  input  b,
  input  a,
  input  Vem1,
  output Vai1,
  output Soma
);

  Adder #(.width(1)) adder_1 (.a(a), .b(b), .out(Soma), .cin(Vem1), .cout(Vai1));
endmodule

// MUX-2
module mux_2 (
  input  Canal0,
  input  Canal1,
  input  Seletor,
  output Saida
);

  wire and_1_out, and_2_out;

  and and_1 (and_1_out, Canal0, ~Seletor);  // AND_Gate
  and and_2 (and_2_out, Canal1, Seletor);
  or or_1 (Saida, and_1_out, and_2_out);
endmodule

module mux_16 (
  input  Canal0,
  input  Canal1,
  input  Canal2,
  input  Canal3,
  input  Canal4,
  input  Canal5,
  input  Canal6,
  input  Canal7,
  input  Canal8,
  input  Canal9,
  input  Canal10,
  input  Canal11,
  input  Canal12,
  input  Canal13,
  input  Canal14,
  input  Canal15,
  input  Seletor3,
  input  Seletor2,
  input  Seletor1,
  input  Seletor0,
  output Saida
);

  wire mux_8_1_out_12, mux_8_2_out_12;

  mux_8 mux_8_1 (
    .Canal0(Canal0), .Canal1(Canal1), .Canal2(Canal2), .Canal3(Canal3), .Canal4(Canal4), .Canal5(Canal5),
    .Canal6(Canal6), .Canal7(Canal7), .Seletor_2(Seletor2), .Seletor_1(Seletor1), .Seletor_0(Seletor0),
    .out_12(mux_8_1_out_12));
  mux_8 mux_8_2 (
    .Canal0(Canal8), .Canal1(Canal9), .Canal2(Canal10), .Canal3(Canal11), .Canal4(Canal12), .Canal5(Canal13),
    .Canal6(Canal14), .Canal7(Canal15), .Seletor_2(Seletor2), .Seletor_1(Seletor1), .Seletor_0(Seletor0),
    .out_12(mux_8_2_out_12));
  mux_2 mux_2_1 (.Canal0(mux_8_1_out_12), .Canal1(mux_8_2_out_12), .Seletor(Seletor3), .Saida(Saida));
endmodule

// Soma
module SomadorCompleto (
  input  b,
  input  a,
  input  vem1,
  output vai1,
  output soma
);

  wire and_1_out, and_2_out, xor_1_out;

  or or_1 (vai1, and_1_out, and_2_out);
  and and_1 (and_1_out, b, a);
  and and_2 (and_2_out, vem1, xor_1_out);
  xor xor_1 (xor_1_out, b, a);
  xor xor_2 (soma, xor_1_out, vem1);
endmodule

// SLL
module sll_32 (
  input  [31:0] in_1,
  input  shift,
  output [31:0] Saida_SLL_32BIT
);

  Multiplexer #(.width(32), .enable("false")) multiplexer_1 (
    .in0(in_1), .in1({in_1[30:0], 1'b0}), .out(Saida_SLL_32BIT), .sel(shift));
endmodule

// SRL
module srl_32 (
  input  [31:0] in_1,
  input  shift,
  output [31:0] Saida_SRL_32BIT
);

  Multiplexer #(.width(32), .enable("false")) multiplexer_1 (
    .in0(in_1), .in1({1'b0, in_1[31:1]}), .out(Saida_SRL_32BIT), .sel(shift));
endmodule

// sll-d
module sll_detect (
  input  [3:0] in_1,
  output out_2
);

  and and_1 (out_2, ~in_1[3], in_1[2], ~in_1[1], in_1[0]);  // AND_Gate
endmodule

// SRA
module sra_32 (
  input  [31:0] in_1,
  input  shift,
  output [31:0] Saida_SRA_32BIT
);

  Multiplexer #(.width(32), .enable("false")) multiplexer_1 (
    .in0(in_1), .in1({{2{in_1[31]}}, in_1[30:1]}), .out(Saida_SRA_32BIT), .sel(shift));
endmodule

// srl-d
module srl_detect (
  input  [3:0] in_1,
  output out_2
);

  and and_1 (out_2, ~in_1[3], in_1[2], in_1[1], ~in_1[0]);  // AND_Gate
endmodule

// sra-d
module sra_detect (
  input  [3:0] in_1,
  output out_2
);

  and and_1 (out_2, ~in_1[3], in_1[2], in_1[1], in_1[0]);  // AND_Gate
endmodule

// Sub
module SubtratorCompleto (
  input  b,
  input  a,
  input  vem1,
  output vai1,
  output s
);

  wire and_1_out, and_2_out, xor_1_out;

  or or_1 (vai1, and_1_out, and_2_out);
  and and_1 (and_1_out, b, ~a);  // AND_Gate
  and and_2 (and_2_out, vem1, ~xor_1_out);  // AND_Gate
  xor xor_1 (xor_1_out, b, a);
  xor xor_2 (s, xor_1_out, vem1);
endmodule

// LUA
module lua_32 (
  input  [31:0] in_1,
  input  shift,
  output [31:0] Saida_LUA_32BIT
);

  Multiplexer #(.width(32), .enable("false")) multiplexer_1 (
    .in0(in_1), .in1({in_1[15:0], {16{1'b0}}}), .out(Saida_LUA_32BIT), .sel(shift));
endmodule

module INFO (
);


  // Notes on the sheet:
  //   0000 - AND
  //   0001 - OR
  //   0010 - XOR
  //   0101 - SLL
  //   0110 - SRL
  //   0111 - SRA
  //   1000 - LUA
  //   1001 - NAND
  //   1111 - C'2
  //   0011 - SOMADOR
  //   0100 - SUBTRATOR
endmodule

// lua-d
module lua_detect (
  input  [3:0] in_1,
  output out_2
);

  and and_1 (out_2, in_1[3], ~in_1[2], ~in_1[1], ~in_1[0]);  // AND_Gate
endmodule

// C'2
module Complemento2 (
  input  B,
  input  Seletor,
  output Saida
);

  wire not_1_out;

  not not_1 (not_1_out, B);
  mux_2 mux_2_1 (.Canal0(B), .Canal1(not_1_out), .Seletor(Seletor), .Saida(Saida));
endmodule

// C'2-d
module C_2_detect (
  input  [3:0] Codigo_operacao,
  output S
);

  and and_1 (S, Codigo_operacao[3], Codigo_operacao[2], Codigo_operacao[1], Codigo_operacao[0]);
endmodule

module demux_2 (
  input  Entrada,
  input  Seletor,
  output out_3,
  output out_4
);

  and and_1 (out_3, Entrada, ~Seletor);  // AND_Gate
  and and_2 (out_4, Entrada, Seletor);
endmodule

module demux_8 (
  input  in_1,
  input  in_2,
  input  in_3,
  input  in_4,
  output out_5,
  output out_6,
  output out_7,
  output out_8,
  output out_9,
  output out_10,
  output out_11,
  output out_12
);

  wire demux_2_1_out_3, demux_2_1_out_4, demux_2_2_out_3, demux_2_2_out_4, demux_2_3_out_3, demux_2_3_out_4;

  demux_2 demux_2_1 (.Entrada(demux_2_2_out_3), .Seletor(in_3), .out_3(demux_2_1_out_3), .out_4(demux_2_1_out_4));
  demux_2 demux_2_2 (.Entrada(in_1), .Seletor(in_2), .out_3(demux_2_2_out_3), .out_4(demux_2_2_out_4));
  demux_2 demux_2_3 (.Entrada(demux_2_2_out_4), .Seletor(in_3), .out_3(demux_2_3_out_3), .out_4(demux_2_3_out_4));
  demux_2 demux_2_4 (.Entrada(demux_2_1_out_3), .Seletor(in_4), .out_3(out_5), .out_4(out_6));
  demux_2 demux_2_5 (.Entrada(demux_2_1_out_4), .Seletor(in_4), .out_3(out_7), .out_4(out_8));
  demux_2 demux_2_6 (.Entrada(demux_2_3_out_3), .Seletor(in_4), .out_3(out_9), .out_4(out_10));
  demux_2 demux_2_7 (.Entrada(demux_2_3_out_4), .Seletor(in_4), .out_3(out_11), .out_4(out_12));
endmodule

// REG
module registrador_32 (
  input  [31:0] Entrada,
  input  Clock,
  output [31:0] Resultado
);

  D_Flip_Flop d_ff_1 (.clk(Clock), .D(Entrada[31]), .Q(Resultado[31]));  // open: Qn, preset, en, reset
  D_Flip_Flop d_ff_2 (.clk(Clock), .D(Entrada[30]), .Q(Resultado[30]));  // open: Qn, preset, en, reset
  D_Flip_Flop d_ff_3 (.clk(Clock), .D(Entrada[29]), .Q(Resultado[29]));  // open: Qn, preset, en, reset
  D_Flip_Flop d_ff_4 (.clk(Clock), .D(Entrada[28]), .Q(Resultado[28]));  // open: Qn, preset, en, reset
  D_Flip_Flop d_ff_5 (.clk(Clock), .D(Entrada[27]), .Q(Resultado[27]));  // open: Qn, preset, en, reset
  D_Flip_Flop d_ff_6 (.clk(Clock), .D(Entrada[26]), .Q(Resultado[26]));  // open: Qn, preset, en, reset
  D_Flip_Flop d_ff_7 (.clk(Clock), .D(Entrada[25]), .Q(Resultado[25]));  // open: Qn, preset, en, reset
  D_Flip_Flop d_ff_8 (.clk(Clock), .D(Entrada[24]), .Q(Resultado[24]));  // open: Qn, preset, en, reset
  D_Flip_Flop d_ff_9 (.clk(Clock), .D(Entrada[23]), .Q(Resultado[23]));  // open: Qn, preset, en, reset
  D_Flip_Flop d_ff_10 (.clk(Clock), .D(Entrada[22]), .Q(Resultado[22]));  // open: Qn, preset, en, reset
  D_Flip_Flop d_ff_11 (.clk(Clock), .D(Entrada[21]), .Q(Resultado[21]));  // open: Qn, preset, en, reset
  D_Flip_Flop d_ff_12 (.clk(Clock), .D(Entrada[20]), .Q(Resultado[20]));  // open: Qn, preset, en, reset
  D_Flip_Flop d_ff_13 (.clk(Clock), .D(Entrada[19]), .Q(Resultado[19]));  // open: Qn, preset, en, reset
  D_Flip_Flop d_ff_14 (.clk(Clock), .D(Entrada[18]), .Q(Resultado[18]));  // open: Qn, preset, en, reset
  D_Flip_Flop d_ff_15 (.clk(Clock), .D(Entrada[17]), .Q(Resultado[17]));  // open: Qn, preset, en, reset
  D_Flip_Flop d_ff_16 (.clk(Clock), .D(Entrada[16]), .Q(Resultado[16]));  // open: Qn, preset, en, reset
  D_Flip_Flop d_ff_17 (.clk(Clock), .D(Entrada[15]), .Q(Resultado[15]));  // open: Qn, preset, en, reset
  D_Flip_Flop d_ff_18 (.clk(Clock), .D(Entrada[14]), .Q(Resultado[14]));  // open: Qn, preset, en, reset
  D_Flip_Flop d_ff_19 (.clk(Clock), .D(Entrada[13]), .Q(Resultado[13]));  // open: Qn, preset, en, reset
  D_Flip_Flop d_ff_20 (.clk(Clock), .D(Entrada[12]), .Q(Resultado[12]));  // open: Qn, preset, en, reset
  D_Flip_Flop d_ff_21 (.clk(Clock), .D(Entrada[11]), .Q(Resultado[11]));  // open: Qn, preset, en, reset
  D_Flip_Flop d_ff_22 (.clk(Clock), .D(Entrada[10]), .Q(Resultado[10]));  // open: Qn, preset, en, reset
  D_Flip_Flop d_ff_23 (.clk(Clock), .D(Entrada[9]), .Q(Resultado[9]));  // open: Qn, preset, en, reset
  D_Flip_Flop d_ff_24 (.clk(Clock), .D(Entrada[8]), .Q(Resultado[8]));  // open: Qn, preset, en, reset
  D_Flip_Flop d_ff_25 (.clk(Clock), .D(Entrada[7]), .Q(Resultado[7]));  // open: Qn, preset, en, reset
  D_Flip_Flop d_ff_26 (.clk(Clock), .D(Entrada[6]), .Q(Resultado[6]));  // open: Qn, preset, en, reset
  D_Flip_Flop d_ff_27 (.clk(Clock), .D(Entrada[5]), .Q(Resultado[5]));  // open: Qn, preset, en, reset
  D_Flip_Flop d_ff_28 (.clk(Clock), .D(Entrada[4]), .Q(Resultado[4]));  // open: Qn, preset, en, reset
  D_Flip_Flop d_ff_29 (.clk(Clock), .D(Entrada[3]), .Q(Resultado[3]));  // open: Qn, preset, en, reset
  D_Flip_Flop d_ff_30 (.clk(Clock), .D(Entrada[2]), .Q(Resultado[2]));  // open: Qn, preset, en, reset
  D_Flip_Flop d_ff_31 (.clk(Clock), .D(Entrada[1]), .Q(Resultado[1]));  // open: Qn, preset, en, reset
  D_Flip_Flop d_ff_32 (.clk(Clock), .D(Entrada[0]), .Q(Resultado[0]));  // open: Qn, preset, en, reset
endmodule

// BR
module bancoRegistrador_32 (
  input  [31:0] DadoExt,
  input  [31:0] DATAin,
  input  Externo,
  input  Clock,
  input  [4:0] SELREG_A,
  input  [4:0] Seletor,
  input  [4:0] SELREG_B,
  output [31:0] REG_A,
  output [31:0] REG_B
);

  wire demultiplexer_1_out0, demultiplexer_1_out1, demultiplexer_1_out2, demultiplexer_1_out3,
       demultiplexer_1_out4, demultiplexer_1_out5, demultiplexer_1_out6, demultiplexer_1_out7,
       demultiplexer_1_out8, demultiplexer_1_out9, demultiplexer_1_out10, demultiplexer_1_out11,
       demultiplexer_1_out12, demultiplexer_1_out13, demultiplexer_1_out14, demultiplexer_1_out15,
       demultiplexer_1_out16, demultiplexer_1_out17, demultiplexer_1_out18, demultiplexer_1_out19,
       demultiplexer_1_out20, demultiplexer_1_out21, demultiplexer_1_out22, demultiplexer_1_out23,
       demultiplexer_1_out24, demultiplexer_1_out25, demultiplexer_1_out26, demultiplexer_1_out27,
       demultiplexer_1_out28, demultiplexer_1_out29, demultiplexer_1_out30, demultiplexer_1_out31;
  wire [31:0] _0_resultado, _1_resultado, _2_resultado, _3_resultado, _4_resultado, _5_resultado,
       _6_resultado, _7_resultado, _8_resultado, _9_resultado, _10_resultado, _11_resultado, _12_resultado,
       _13_resultado, _14_resultado, _15_resultado, _16_resultado, _17_resultado, _18_resultado,
       _19_resultado, _20_resultado, _21_resultado, _22_resultado, _23_resultado, _24_resultado,
       _25_resultado, _26_resultado, _27_resultado, _28_resultado, _29_resultado, _30_resultado,
       _31_resultado, multiplexer_1_out;

  Demultiplexer #(.select(5), .enable("false")) demultiplexer_1 (
    .out0(demultiplexer_1_out0), .out1(demultiplexer_1_out1), .out2(demultiplexer_1_out2),
    .out3(demultiplexer_1_out3), .out4(demultiplexer_1_out4), .out5(demultiplexer_1_out5),
    .out6(demultiplexer_1_out6), .out7(demultiplexer_1_out7), .out8(demultiplexer_1_out8),
    .out9(demultiplexer_1_out9), .out10(demultiplexer_1_out10), .out11(demultiplexer_1_out11),
    .out12(demultiplexer_1_out12), .out13(demultiplexer_1_out13), .out14(demultiplexer_1_out14),
    .out15(demultiplexer_1_out15), .out16(demultiplexer_1_out16), .out17(demultiplexer_1_out17),
    .out18(demultiplexer_1_out18), .out19(demultiplexer_1_out19), .out20(demultiplexer_1_out20),
    .out21(demultiplexer_1_out21), .out22(demultiplexer_1_out22), .out23(demultiplexer_1_out23),
    .out24(demultiplexer_1_out24), .out25(demultiplexer_1_out25), .out26(demultiplexer_1_out26),
    .out27(demultiplexer_1_out27), .out28(demultiplexer_1_out28), .out29(demultiplexer_1_out29),
    .out30(demultiplexer_1_out30), .out31(demultiplexer_1_out31), .in(Clock), .sel(Seletor));
  Multiplexer #(.width(32), .enable("false")) multiplexer_1 (
    .in0(DadoExt), .in1(DATAin), .out(multiplexer_1_out), .sel(Externo));
  registrador_32 _0 (.Entrada(multiplexer_1_out), .Clock(demultiplexer_1_out0), .Resultado(_0_resultado));
  registrador_32 _1 (.Entrada(multiplexer_1_out), .Clock(demultiplexer_1_out1), .Resultado(_1_resultado));
  registrador_32 _2 (.Entrada(multiplexer_1_out), .Clock(demultiplexer_1_out2), .Resultado(_2_resultado));
  registrador_32 _3 (.Entrada(multiplexer_1_out), .Clock(demultiplexer_1_out3), .Resultado(_3_resultado));
  registrador_32 _4 (.Entrada(multiplexer_1_out), .Clock(demultiplexer_1_out4), .Resultado(_4_resultado));
  registrador_32 _5 (.Entrada(multiplexer_1_out), .Clock(demultiplexer_1_out5), .Resultado(_5_resultado));
  registrador_32 _6 (.Entrada(multiplexer_1_out), .Clock(demultiplexer_1_out6), .Resultado(_6_resultado));
  registrador_32 _7 (.Entrada(multiplexer_1_out), .Clock(demultiplexer_1_out7), .Resultado(_7_resultado));
  registrador_32 _8 (.Entrada(multiplexer_1_out), .Clock(demultiplexer_1_out8), .Resultado(_8_resultado));
  registrador_32 _9 (.Entrada(multiplexer_1_out), .Clock(demultiplexer_1_out9), .Resultado(_9_resultado));
  registrador_32 _10 (.Entrada(multiplexer_1_out), .Clock(demultiplexer_1_out10), .Resultado(_10_resultado));
  registrador_32 _11 (.Entrada(multiplexer_1_out), .Clock(demultiplexer_1_out11), .Resultado(_11_resultado));
  registrador_32 _12 (.Entrada(multiplexer_1_out), .Clock(demultiplexer_1_out12), .Resultado(_12_resultado));
  registrador_32 _13 (.Entrada(multiplexer_1_out), .Clock(demultiplexer_1_out13), .Resultado(_13_resultado));
  registrador_32 _14 (.Entrada(multiplexer_1_out), .Clock(demultiplexer_1_out14), .Resultado(_14_resultado));
  registrador_32 _15 (.Entrada(multiplexer_1_out), .Clock(demultiplexer_1_out15), .Resultado(_15_resultado));
  registrador_32 _16 (.Entrada(multiplexer_1_out), .Clock(demultiplexer_1_out16), .Resultado(_16_resultado));
  registrador_32 _17 (.Entrada(multiplexer_1_out), .Clock(demultiplexer_1_out17), .Resultado(_17_resultado));
  registrador_32 _18 (.Entrada(multiplexer_1_out), .Clock(demultiplexer_1_out18), .Resultado(_18_resultado));
  registrador_32 _19 (.Entrada(multiplexer_1_out), .Clock(demultiplexer_1_out19), .Resultado(_19_resultado));
  registrador_32 _20 (.Entrada(multiplexer_1_out), .Clock(demultiplexer_1_out20), .Resultado(_20_resultado));
  registrador_32 _21 (.Entrada(multiplexer_1_out), .Clock(demultiplexer_1_out21), .Resultado(_21_resultado));
  registrador_32 _22 (.Entrada(multiplexer_1_out), .Clock(demultiplexer_1_out22), .Resultado(_22_resultado));
  registrador_32 _23 (.Entrada(multiplexer_1_out), .Clock(demultiplexer_1_out23), .Resultado(_23_resultado));
  registrador_32 _24 (.Entrada(multiplexer_1_out), .Clock(demultiplexer_1_out24), .Resultado(_24_resultado));
  registrador_32 _25 (.Entrada(multiplexer_1_out), .Clock(demultiplexer_1_out25), .Resultado(_25_resultado));
  registrador_32 _26 (.Entrada(multiplexer_1_out), .Clock(demultiplexer_1_out26), .Resultado(_26_resultado));
  registrador_32 _27 (.Entrada(multiplexer_1_out), .Clock(demultiplexer_1_out27), .Resultado(_27_resultado));
  registrador_32 _28 (.Entrada(multiplexer_1_out), .Clock(demultiplexer_1_out28), .Resultado(_28_resultado));
  registrador_32 _29 (.Entrada(multiplexer_1_out), .Clock(demultiplexer_1_out29), .Resultado(_29_resultado));
  registrador_32 _30 (.Entrada(multiplexer_1_out), .Clock(demultiplexer_1_out30), .Resultado(_30_resultado));
  registrador_32 _31 (.Entrada(multiplexer_1_out), .Clock(demultiplexer_1_out31), .Resultado(_31_resultado));
  Multiplexer #(.select(5), .width(32), .enable("false")) multiplexer_2 (
    .in0(_0_resultado), .in1(_1_resultado), .in2(_2_resultado), .in3(_3_resultado), .in4(_4_resultado),
    .in5(_5_resultado), .in6(_6_resultado), .in7(_7_resultado), .in8(_8_resultado), .in9(_9_resultado),
    .in10(_10_resultado), .in11(_11_resultado), .in12(_12_resultado), .in13(_13_resultado),
    .in14(_14_resultado), .in15(_15_resultado), .in16(_16_resultado), .in17(_17_resultado),
    .in18(_18_resultado), .in19(_19_resultado), .in20(_20_resultado), .in21(_21_resultado),
    .in22(_22_resultado), .in23(_23_resultado), .in24(_24_resultado), .in25(_25_resultado),
    .in26(_26_resultado), .in27(_27_resultado), .in28(_28_resultado), .in29(_29_resultado),
    .in30(_30_resultado), .in31(_31_resultado), .out(REG_A), .sel(SELREG_A));
  Multiplexer #(.select(5), .width(32), .enable("false")) multiplexer_3 (
    .in0(_0_resultado), .in1(_1_resultado), .in2(_2_resultado), .in3(_3_resultado), .in4(_4_resultado),
    .in5(_5_resultado), .in6(_6_resultado), .in7(_7_resultado), .in8(_8_resultado), .in9(_9_resultado),
    .in10(_10_resultado), .in11(_11_resultado), .in12(_12_resultado), .in13(_13_resultado),
    .in14(_14_resultado), .in15(_15_resultado), .in16(_16_resultado), .in17(_17_resultado),
    .in18(_18_resultado), .in19(_19_resultado), .in20(_20_resultado), .in21(_21_resultado),
    .in22(_22_resultado), .in23(_23_resultado), .in24(_24_resultado), .in25(_25_resultado),
    .in26(_26_resultado), .in27(_27_resultado), .in28(_28_resultado), .in29(_29_resultado),
    .in30(_30_resultado), .in31(_31_resultado), .out(REG_B), .sel(SELREG_B));
endmodule
